// Logisim project Counters001E.circ as structural Verilog: 4 circuits, main circuit Counter_T
module Counter_T (
);

  wire and_1_out, B_q, C_q, clock_1_out;

  and and_1 (and_1_out, B_q, C_q);
  Clock clock_1 (.out(clock_1_out));
  T_Flip_Flop A (.T(and_1_out), .clk(clock_1_out));  // open: Q, Qn, reset, preset
  T_Flip_Flop B (.T(C_q), .clk(clock_1_out), .Q(B_q));  // open: Qn, reset, preset
  T_Flip_Flop C (.T(clock_1_out), .clk(clock_1_out), .Q(C_q));  // open: Qn, reset, preset
endmodule

module Counter_D (
);

  wire A_q, and_1_out, B_q, C_q, C_qn, clock_1_out, xor_1_out, xor_2_out;

  and and_1 (and_1_out, B_q, C_q);
  Clock clock_1 (.out(clock_1_out));
  xor xor_1 (xor_1_out, and_1_out, A_q);
  D_Flip_Flop A (.D(xor_1_out), .clk(clock_1_out), .Q(A_q));  // open: Qn, preset, reset
  D_Flip_Flop B (.D(xor_2_out), .clk(clock_1_out), .Q(B_q));  // open: Qn, preset, reset
  xor xor_2 (xor_2_out, C_q, B_q);
  D_Flip_Flop C (.D(C_qn), .clk(clock_1_out), .Q(C_q), .Qn(C_qn));  // open: preset, reset
endmodule

module Counter_SR (
);

  wire A_q, A_qn, and_1_out, and_2_out, and_3_out, and_4_out, B_q, B_qn, C_q, C_qn, clock_1_out;

  Clock clock_1 (.out(clock_1_out));
  S_R_Flip_Flop A (.S(and_1_out), .R(and_2_out), .clk(clock_1_out), .Q(A_q), .Qn(A_qn));  // open: reset, preset
  and and_1 (and_1_out, A_qn, and_4_out);
  and and_2 (and_2_out, and_4_out, A_q);
  and and_3 (and_3_out, C_q, B_qn);
  and and_4 (and_4_out, C_q, B_q);
  S_R_Flip_Flop B (.S(and_3_out), .R(and_4_out), .clk(clock_1_out), .Q(B_q), .Qn(B_qn));  // open: reset, preset
  S_R_Flip_Flop C (.S(C_qn), .R(C_q), .clk(clock_1_out), .Q(C_q), .Qn(C_qn));  // open: reset, preset
endmodule

module Counter_LST (
  input  Reset,
  input  Load_Count,
  input  Direction,
  input  [7:0] in_4,
  output out_5,
  output [7:0] out_6
);

  wire clock_1_out;

  Clock clock_1 (.out(clock_1_out));
  Counter counter_1 (
    .clr(Reset), .load(Load_Count), .up(Direction), .clk(clock_1_out), .D(in_4), .carry(out_5), .Q(out_6));  // open: count
endmodule
