// Logisim project Counters002E.circ as structural Verilog: 1 circuit, main circuit main
module main (
);

  wire A_q, A_qn, and_1_out, and_2_out, and_3_out, B_q, B_qn, C_q, clock_1_out, or_1_out, or_2_out;

  Clock clock_1 (.out(clock_1_out));
  and and_1 (and_1_out, B_q, C_q);
  or or_1 (or_1_out, and_1_out, A_qn);
  D_Flip_Flop A (.D(or_1_out), .clk(clock_1_out), .Q(A_q), .Qn(A_qn));  // open: preset, reset
  and and_2 (and_2_out, B_qn, C_q);
  D_Flip_Flop B (.D(and_2_out), .clk(clock_1_out), .Q(B_q), .Qn(B_qn));  // open: preset, reset
  and and_3 (and_3_out, C_q, B_qn);
  or or_2 (or_2_out, and_3_out, A_q);
  D_Flip_Flop C (.D(or_2_out), .clk(clock_1_out), .Q(C_q));  // open: Qn, preset, reset

  // Notes on the sheet:
  //   001  111   101   011   100
endmodule
