// Logisim project Homework10.circ as structural Verilog: 5 circuits, main circuit main
module main (
  input  [7:0] in_1,
  input  [7:0] in_2,
  input  Reset,
  input  Load,
  input  Multiply,
  input  in_6,
  input  in_7,
  output [7:0] out_8,
  output out_9,
  output out_10,
  output [7:0] out_11,
  output out_12
);

  wire clock_1_out;
  wire [7:0] adder_1_out, multiplexer_1_out, register_1_q;

  Clock clock_1 (.out(clock_1_out));
  // Shift_Register shift_register_1: pin names not known; wires that end beside it: Reset, Load, Multiply, clock_1_out, in_6, in_2[7], in_2[6], in_2[5], in_2[4], in_2[3], out_8[7], out_8[6], out_8[5], out_8[4], out_8[3]
  // Shift_Register shift_register_2: pin names not known; wires that end beside it: in_2[2], in_2[1], in_2[0], Reset, Load, Multiply, clock_1_out, in_7, in_1[0], in_1[1], in_1[2], in_1[3], in_1[4], in_1[5], in_1[6], in_1[7], out_8[2], out_8[1], out_8[0], out_11[0], out_11[1], out_11[2], out_11[3], out_11[4], out_11[5], out_11[6], out_11[7]
  Multiplexer #(.width(8), .enable("false")) multiplexer_1 (
    .in0({8{1'b0}}), .in1(out_11), .out(multiplexer_1_out), .sel(out_8[0]));
  Adder adder_1 (.a(multiplexer_1_out), .b(register_1_q), .out(adder_1_out), .cin(1'b0), .cout(out_10));
  Register register_1 (.D(adder_1_out), .clk(clock_1_out), .Q(register_1_q), .clr(Reset));  // open: en

  assign out_9 = out_8[0];
  assign out_12 = out_11[7];

  // Notes on the sheet:
  //   Daniel Weitman
  //   A
  //   B
  //   Clock
  //   B
  //   A
endmodule

module Sequence001011 (
  input  Reset,
  output Sequence
);

  wire and_1_out, and_2_out, and_3_out, and_4_out, clock_1_out, d_ff_1_qn, d_ff_2_q, d_ff_2_qn, d_ff_3_q,
       d_ff_3_qn, or_1_out;

  Clock clock_1 (.out(clock_1_out));
  D_Flip_Flop d_ff_1 (.D(or_1_out), .clk(clock_1_out), .Q(Sequence), .Qn(d_ff_1_qn), .reset(Reset));  // open: preset
  D_Flip_Flop d_ff_2 (.D(and_3_out), .clk(clock_1_out), .Q(d_ff_2_q), .Qn(d_ff_2_qn), .reset(Reset));  // open: preset
  D_Flip_Flop d_ff_3 (.D(and_4_out), .clk(clock_1_out), .Q(d_ff_3_q), .Qn(d_ff_3_qn), .reset(Reset));  // open: preset
  and and_1 (and_1_out, d_ff_2_qn, d_ff_3_q);
  and and_2 (and_2_out, d_ff_1_qn, d_ff_2_q, d_ff_3_qn);
  and and_3 (and_3_out, Sequence, d_ff_2_qn);
  and and_4 (and_4_out, d_ff_1_qn, d_ff_3_qn);
  or or_1 (or_1_out, and_1_out, and_2_out);

  // Notes on the sheet:
  //   Daniel Weitman
  //   Clock
  //   _
  //   _
  //   _
  //   BC
  //   _
  //   ABC
  //   _
  //   AB
  //   _
  //   AC
  //   |
  //   0
  //   |
  //   |
  //   0
  //   |
  //   |
  //   0
  //   |
  //   |
  //   0
  //   |
  //   |
  //   1
  //   |
  //   |
  //   1
  //   |
  //   |
  //   1
  //   |
  //   |
  //   1
  //   _
  //   A
  //   \_______
  //   _
  //   _
  //   |
  //   |
  //   0
  //   BC
  //   _______
  //   |
  //   |
  //   _
  //   |
  //   |
  //   |
  //   BC
  //   1
  //   |
  //   _______
  //   _______
  //   |
  //   |
  //   BC
  //   0
  //   |
  //   _______
  //   |
  //   _
  //   |
  //   |
  //   1
  //   BC
  //   |
  //   |
  //   |
  //   _______
  //   |
  //   0
  //   0
  //   0
  //   |
  //   |
  //   1
  //   1
  //   0
  //   |
  //   0
  //   1
  //   |
  //   1
  //   |
  //   |
  //   1
  //   0
  //   1
  //   |
  //   |
  //   0
  //   0
  //   0
  //   |
  //   |
  //   1
  //   1
  //   0
  //   |
  //   |
  //   0
  //   1
  //   |
  //   |
  //   1
  //   1
  //   A
  //   _
  //   |
  //   0
  //   BC
  //   _
  //   |
  //   |
  //   1
  //   BC
  //   |
  //   |
  //   BC
  //   0
  //   |
  //   |
  //   BC
  //   0
  //   |
  //   000-->001-->100-->010-->101-->110-->000
  //   | A | B | C | A+ | B+ | C+ | DA | DB | DC |
  //   ________________________________
  //   0
  //   0
  //   0
  //   0
  //   1
  //   1
  //   0
  //   0
  //   0
  //   0
  //   _
  //   A
  //   A
  //   \_______
  //   _
  //   |
  //   |
  //   0
  //   1
  //   _______
  //   |
  //   |
  //   |
  //   |
  //   1
  //   |
  //   0
  //   |
  //   _______
  //   _______
  //   |
  //   |
  //   0
  //   0
  //   |
  //   _______
  //   |
  //   _
  //   |
  //   |
  //   0
  //   |
  //   0
  //   |
  //   |
  //   _______
  //   |
  //   1
  //   0
  //   |
  //   |
  //   0
  //   1
  //   |
  //   1
  //   1
  //   |
  //   |
  //   |
  //   0
  //   0
  //   |
  //   |
  //   0
  //   0
  //   |
  //   |
  //   0
  //   1
  //   |
  //   |
  //   0
  //   0
  //   |
  //   0
  //   |
  //   0
  //   _
  //   _
  //   |
  //   |
  //   BC
  //   |
  //   |
  //   _
  //   |
  //   |
  //   |
  //   BC
  //   |
  //   |
  //   |
  //   |
  //   BC
  //   |
  //   |
  //   _
  //   |
  //   |
  //   BC
  //   |
  //   |
  //   |
  //   |
  //   1
  //   0
  //   |
  //   |
  //   0
  //   0
  //   |
  //   1
  //   |
  //   0
  //   |
  //   |
  //   0
  //   0
  //   |
  //   |
  //   0
  //   1
  //   |
  //   |
  //   1
  //   0
  //   |
  //   |
  //   0
  //   0
  //   |
  //   |
  //   0
  //   0
  //   _
  //   A
  //   A
  //   \_______
  //   |
  //   |
  //   1
  //   0
  //   _______
  //   |
  //   |
  //   |
  //   |
  //   0
  //   0
  //   _______
  //   _______
  //   |
  //   |
  //   |
  //   0
  //   0
  //   |
  //   _______
  //   |
  //   |
  //   |
  //   1
  //   0
  //   |
  //   _______
  //   |
endmodule

module Sequence1326754 (
  input  Reset,
  input  Reset_2
);

  wire and_1_out, and_2_out, and_3_out, and_4_out, and_5_out, and_6_out, and_7_out, and_8_out, and_9_out,
       and_10_out, and_11_out, and_12_out, and_13_out, clock_1_out, clock_2_out, d_ff_1_q, d_ff_1_qn,
       d_ff_2_q, d_ff_2_qn, d_ff_3_q, d_ff_3_qn, or_1_out, or_2_out, or_3_out, or_4_out, or_5_out, or_6_out,
       t_ff_1_q, t_ff_1_qn, t_ff_2_q, t_ff_2_qn, t_ff_3_q, t_ff_3_qn;

  Clock clock_1 (.out(clock_1_out));
  Clock clock_2 (.out(clock_2_out));
  D_Flip_Flop d_ff_1 (.D(or_1_out), .clk(clock_1_out), .Q(d_ff_1_q), .Qn(d_ff_1_qn), .reset(Reset));  // open: preset
  T_Flip_Flop t_ff_1 (.T(or_4_out), .clk(clock_2_out), .Q(t_ff_1_q), .Qn(t_ff_1_qn), .reset(Reset_2));  // open: preset
  D_Flip_Flop d_ff_2 (.D(or_2_out), .clk(clock_1_out), .Q(d_ff_2_q), .Qn(d_ff_2_qn), .reset(Reset));  // open: preset
  T_Flip_Flop t_ff_2 (.T(or_5_out), .clk(clock_2_out), .Q(t_ff_2_q), .Qn(t_ff_2_qn), .reset(Reset_2));  // open: preset
  D_Flip_Flop d_ff_3 (.D(or_3_out), .clk(clock_1_out), .Q(d_ff_3_q), .Qn(d_ff_3_qn), .reset(Reset));  // open: preset
  T_Flip_Flop t_ff_3 (.T(or_6_out), .clk(clock_2_out), .Q(t_ff_3_q), .Qn(t_ff_3_qn), .reset(Reset_2));  // open: preset
  and and_1 (and_1_out, d_ff_1_q, d_ff_3_q);
  and and_2 (and_2_out, d_ff_2_q, d_ff_3_qn);
  and and_3 (and_3_out, d_ff_2_q, d_ff_3_qn);
  and and_4 (and_4_out, d_ff_1_q, d_ff_2_q);
  and and_5 (and_5_out, d_ff_2_qn, d_ff_3_qn);
  and and_6 (and_6_out, d_ff_1_qn, d_ff_2_qn);
  and and_7 (and_7_out, t_ff_1_q, t_ff_2_qn, t_ff_3_qn);
  and and_8 (and_8_out, t_ff_1_qn, t_ff_2_q, t_ff_3_qn);
  and and_9 (and_9_out, t_ff_1_qn, t_ff_2_qn, t_ff_3_q);
  and and_10 (and_10_out, t_ff_1_q, t_ff_2_q, t_ff_3_q);
  and and_11 (and_11_out, t_ff_1_qn, t_ff_2_q, t_ff_3_q);
  and and_12 (and_12_out, t_ff_1_q, t_ff_2_qn);
  and and_13 (and_13_out, t_ff_1_q, t_ff_3_qn);
  or or_1 (or_1_out, and_1_out, and_2_out);
  or or_2 (or_2_out, and_3_out, d_ff_1_qn);
  or or_3 (or_3_out, and_4_out, and_5_out, and_6_out);
  or or_4 (or_4_out, and_7_out, and_8_out);
  or or_5 (or_5_out, and_9_out, and_10_out);
  or or_6 (or_6_out, and_11_out, and_12_out, and_13_out);

  // Notes on the sheet:
  //   Clock
  //   Clock
  //   Daniel Weitman
endmodule

module Templates (
);


  // Notes on the sheet:
  //   Daniel Weitman
  //   _
  //   A
  //   _
  //   _
  //   |
  //   BC
  //   |
  //   _
  //   |
  //   |
  //   BC
  //   |
  //   |
  //   BC
  //   |
  //   _
  //   |
  //   BC
  //   |
  //   |
  //   A
  //   \_______
  //   |
  //   |
  //   _______
  //   |
  //   |
  //   |
  //   |
  //   _______
  //   _______
  //   |
  //   |
  //   |
  //   |
  //   _______
  //   |
  //   |
  //   |
  //   |
  //   _______
  //   |
  //   |
  //   0
  //   0
  //   |
  //   |
  //   0
  //   0
  //   |
  //   0
  //   1
  //   |
  //   |
  //   |
  //   1
  //   0
  //   |
  //   |
  //   0
  //   1
  //   |
  //   |
  //   0
  //   1
  //   |
  //   |
  //   1
  //   1
  //   |
  //   |
  //   1
  //   1
  //   |
  //   0
  //   |
  //   |
  //   1
  //   |
  //   0
  //   |
  //   |
  //   |
  //   1
  //   |
  //   |
  //   0
  //   |
  //   |
  //   1
  //   |
  //   |
  //   0
  //   |
  //   1
  //   |
  //   | A | B | C | A+ | B+ | C+ |    |    |    |
  //   ________________________________
  //   |
  //   |
  //   |
  //   |
  //   |
  //   |
  //   |
  //   |
  //   |
  //   |
  //   |
  //   |
  //   |
  //   |
  //   |
endmodule

module Sequence1234567890 (
  input  Reset,
  input  Reset_2
);

  wire and_1_out, and_2_out, and_3_out, and_4_out, and_5_out, and_6_out, and_7_out, and_8_out, and_9_out,
       and_10_out, and_11_out, and_12_out, and_13_out, and_14_out, and_15_out, and_16_out, clock_1_out,
       clock_2_out, d_ff_1_q, d_ff_1_qn, d_ff_2_q, d_ff_2_qn, d_ff_3_q, d_ff_3_qn, d_ff_4_q, d_ff_4_qn,
       j_k_ff_1_q, j_k_ff_1_qn, j_k_ff_2_q, j_k_ff_2_qn, j_k_ff_3_q, j_k_ff_3_qn, j_k_ff_4_q, or_1_out,
       or_2_out, or_3_out, or_4_out, or_5_out, or_6_out, or_7_out, or_8_out;

  Clock clock_1 (.out(clock_1_out));
  Clock clock_2 (.out(clock_2_out));
  D_Flip_Flop d_ff_1 (.D(or_1_out), .clk(clock_1_out), .Q(d_ff_1_q), .Qn(d_ff_1_qn), .reset(Reset));  // open: preset
  J_K_Flip_Flop j_k_ff_1 (
    .J(and_10_out), .K(or_5_out), .clk(clock_2_out), .Q(j_k_ff_1_q), .Qn(j_k_ff_1_qn), .reset(Reset_2));  // open: preset
  D_Flip_Flop d_ff_2 (.D(or_2_out), .clk(clock_1_out), .Q(d_ff_2_q), .Qn(d_ff_2_qn), .reset(Reset));  // open: preset
  J_K_Flip_Flop j_k_ff_2 (
    .J(and_13_out), .K(or_6_out), .clk(clock_2_out), .Q(j_k_ff_2_q), .Qn(j_k_ff_2_qn), .reset(Reset_2));  // open: preset
  D_Flip_Flop d_ff_3 (.D(or_3_out), .clk(clock_1_out), .Q(d_ff_3_q), .Qn(d_ff_3_qn), .reset(Reset));  // open: preset
  J_K_Flip_Flop j_k_ff_3 (
    .J(and_15_out), .K(or_7_out), .clk(clock_2_out), .Q(j_k_ff_3_q), .Qn(j_k_ff_3_qn), .reset(Reset_2));  // open: preset
  D_Flip_Flop d_ff_4 (.D(or_4_out), .clk(clock_1_out), .Q(d_ff_4_q), .Qn(d_ff_4_qn), .reset(Reset));  // open: preset
  J_K_Flip_Flop j_k_ff_4 (
    .J(or_8_out), .K(1'b1), .clk(clock_2_out), .Q(j_k_ff_4_q), .reset(Reset_2));  // open: Qn, preset
  and and_1 (and_1_out, d_ff_1_qn, d_ff_2_q, d_ff_3_q, d_ff_4_q);
  or or_1 (or_1_out, and_1_out, and_2_out);
  and and_2 (and_2_out, d_ff_1_q, d_ff_2_qn, d_ff_3_qn, d_ff_4_qn);
  and and_3 (and_3_out, d_ff_1_qn, d_ff_2_q, d_ff_3_qn);
  and and_4 (and_4_out, d_ff_1_qn, d_ff_2_q, d_ff_4_qn);
  or or_2 (or_2_out, and_3_out, and_4_out, and_5_out);
  and and_5 (and_5_out, d_ff_1_qn, d_ff_2_qn, d_ff_3_q, d_ff_4_q);
  and and_6 (and_6_out, d_ff_1_qn, d_ff_3_qn, d_ff_4_q);
  or or_3 (or_3_out, and_6_out, and_7_out);
  and and_7 (and_7_out, d_ff_1_qn, d_ff_3_q, d_ff_4_qn);
  and and_8 (and_8_out, d_ff_1_qn, d_ff_4_qn);
  or or_4 (or_4_out, and_8_out, and_9_out);
  and and_9 (and_9_out, d_ff_2_qn, d_ff_3_qn, d_ff_4_qn);
  and and_10 (and_10_out, j_k_ff_2_q, j_k_ff_3_q, j_k_ff_4_q);
  and and_11 (and_11_out, j_k_ff_2_q, j_k_ff_3_qn);
  or or_5 (or_5_out, and_11_out, j_k_ff_3_q, and_12_out);
  and and_12 (and_12_out, j_k_ff_1_q, j_k_ff_4_q);
  and and_13 (and_13_out, j_k_ff_1_qn, j_k_ff_3_q, j_k_ff_4_q);
  and and_14 (and_14_out, j_k_ff_3_q, j_k_ff_4_q);
  or or_6 (or_6_out, and_14_out, j_k_ff_1_q);
  and and_15 (and_15_out, j_k_ff_1_qn, j_k_ff_4_q);
  or or_7 (or_7_out, j_k_ff_1_q, j_k_ff_4_q);
  and and_16 (and_16_out, j_k_ff_2_qn, j_k_ff_3_qn);
  or or_8 (or_8_out, and_16_out, j_k_ff_1_qn);

  // Notes on the sheet:
  //   Daniel Weitman
  //   Clock
  //   Clock
endmodule
