// Logisim project Register001E.circ as structural Verilog: 8 circuits, main circuit Reg4bGC
module Reg4bGC (
  input  [3:0] Data,
  input  Clear,
  input  Load,
  output [3:0] Storage
);

  wire and_1_out, clock_1_out;

  Clock clock_1 (.out(clock_1_out));
  and and_1 (and_1_out, Load, clock_1_out);
  D_Flip_Flop d_ff_1 (.D(Data[3]), .clk(and_1_out), .Q(Storage[3]), .reset(Clear));  // open: Qn, preset
  D_Flip_Flop d_ff_2 (.D(Data[2]), .clk(and_1_out), .Q(Storage[2]), .reset(Clear));  // open: Qn, preset
  D_Flip_Flop d_ff_3 (.D(Data[1]), .clk(and_1_out), .Q(Storage[1]), .reset(Clear));  // open: Qn, preset
  D_Flip_Flop d_ff_4 (.D(Data[0]), .clk(and_1_out), .Q(Storage[0]), .reset(Clear));  // open: Qn, preset
endmodule

module Reg4bDT (
  input  Clear_A,
  input  Clear_B,
  input  Control
);

  wire and_1_out, and_2_out, and_3_out, and_4_out, and_5_out, and_6_out, and_7_out, and_8_out, clock_1_out,
       d_ff_1_q, d_ff_2_q, d_ff_3_q, d_ff_4_q, d_ff_7_q, d_ff_8_q, d_ff_9_q, d_ff_10_q, not_1_out, or_1_out;

  Clock clock_1 (.out(clock_1_out));
  D_Flip_Flop d_ff_1 (.clk(clock_1_out), .Q(d_ff_1_q), .reset(Clear_A));  // open: D, Qn, preset
  D_Flip_Flop d_ff_2 (.clk(clock_1_out), .Q(d_ff_2_q), .reset(Clear_B));  // open: D, Qn, preset
  not not_1 (not_1_out, Control);
  and and_1 (and_1_out, d_ff_1_q, not_1_out);
  and and_2 (and_2_out, d_ff_2_q, Control);
  D_Flip_Flop d_ff_3 (.clk(clock_1_out), .Q(d_ff_3_q), .reset(Clear_A));  // open: D, Qn, preset
  D_Flip_Flop d_ff_4 (.clk(clock_1_out), .Q(d_ff_4_q), .reset(Clear_B));  // open: D, Qn, preset
  D_Flip_Flop d_ff_5 (.D(or_1_out), .clk(clock_1_out));  // open: Q, Qn, preset, reset
  or or_1 (or_1_out, and_1_out, and_2_out);
  and and_3 (and_3_out, d_ff_3_q, not_1_out);
  D_Flip_Flop d_ff_6 (.clk(and_3_out), .D(and_4_out));  // open: Q, Qn, preset, reset
  // OR_Gate or_2 has open pins: in0=and_3_out, in1=and_4_out, out=open
  and and_4 (and_4_out, d_ff_4_q, Control);
  D_Flip_Flop d_ff_7 (.clk(clock_1_out), .Q(d_ff_7_q), .reset(Clear_A));  // open: D, Qn, preset
  D_Flip_Flop d_ff_8 (.clk(clock_1_out), .Q(d_ff_8_q), .reset(Clear_B));  // open: D, Qn, preset
  and and_5 (and_5_out, d_ff_7_q, not_1_out);
  and and_6 (and_6_out, d_ff_8_q, Control);
  D_Flip_Flop d_ff_9 (.clk(clock_1_out), .Q(d_ff_9_q), .reset(Clear_A));  // open: D, Qn, preset
  D_Flip_Flop d_ff_10 (.clk(clock_1_out), .Q(d_ff_10_q), .reset(Clear_B));  // open: D, Qn, preset
  D_Flip_Flop d_ff_11 (.clk(and_5_out), .D(and_6_out));  // open: Q, Qn, preset, reset
  // OR_Gate or_3 has open pins: in0=and_5_out, in1=and_6_out, out=open
  and and_7 (and_7_out, d_ff_9_q, not_1_out);
  and and_8 (and_8_out, d_ff_10_q, Control);
  D_Flip_Flop d_ff_12 (.clk(and_7_out), .D(and_8_out));  // open: Q, Qn, preset, reset
  // OR_Gate or_4 has open pins: in0=and_7_out, in1=and_8_out, out=open
endmodule

module RegDT (
  input  [7:0] in_1,
  input  [7:0] in_2,
  input  [7:0] in_3,
  input  [7:0] in_4,
  input  in_5,
  input  [1:0] in_6,
  output [7:0] out_7
);

  wire clock_1_out;
  wire [7:0] multiplexer_1_out, Register_0_q, Register_1_q, Register_2_q, Register_3_q;

  Register #(.trigger("high")) Register_3 (.D(in_1), .clk(in_5), .Q(Register_3_q));  // open: en, clr
  Register #(.trigger("high")) Register_2 (.D(in_2), .clk(in_5), .Q(Register_2_q));  // open: en, clr
  Register #(.trigger("high")) Register_1 (.D(in_3), .clk(in_5), .Q(Register_1_q));  // open: en, clr
  Register #(.trigger("high")) Register_0 (.D(in_4), .clk(in_5), .Q(Register_0_q));  // open: en, clr
  Multiplexer #(.select(2), .width(8), .enable("false")) multiplexer_1 (
    .in0(Register_0_q), .in1(Register_1_q), .in2(Register_2_q), .in3(Register_3_q), .out(multiplexer_1_out),
    .sel(in_6));
  Register Register_A (.D(multiplexer_1_out), .clk(clock_1_out), .Q(out_7));  // open: en, clr
  Clock clock_1 (.out(clock_1_out));
endmodule

module RegDT2 (
  input  [7:0] in_1,
  input  [7:0] in_2,
  input  [7:0] in_3,
  input  [7:0] in_4,
  input  in_5,
  input  [1:0] in_6,
  input  [1:0] in_7,
  output [7:0] out_8,
  output [7:0] out_9,
  output [7:0] out_10,
  output [7:0] out_11
);

  wire clock_1_out;
  wire [7:0] demultiplexer_1_out0, demultiplexer_1_out1, demultiplexer_1_out2, demultiplexer_1_out3,
       multiplexer_1_out, Register_0_q, Register_1_q, Register_2_q, Register_3_q;

  Clock clock_1 (.out(clock_1_out));
  Register #(.trigger("high")) Register_3 (.D(in_1), .clk(in_5), .Q(Register_3_q));  // open: en, clr
  Register Register_D (.D(demultiplexer_1_out3), .clk(clock_1_out), .Q(out_8));  // open: en, clr
  Register #(.trigger("high")) Register_2 (.D(in_2), .clk(in_5), .Q(Register_2_q));  // open: en, clr
  Register Register_C (.D(demultiplexer_1_out2), .clk(clock_1_out), .Q(out_9));  // open: en, clr
  Register #(.trigger("high")) Register_1 (.D(in_3), .clk(in_5), .Q(Register_1_q));  // open: en, clr
  Register Register_B (.D(demultiplexer_1_out1), .clk(clock_1_out), .Q(out_10));  // open: en, clr
  Register #(.trigger("high")) Register_0 (.D(in_4), .clk(in_5), .Q(Register_0_q));  // open: en, clr
  Register Register_A (.D(demultiplexer_1_out0), .clk(clock_1_out), .Q(out_11));  // open: en, clr
  Multiplexer #(.select(2), .width(8), .enable("false")) multiplexer_1 (
    .in0(Register_0_q), .in1(Register_1_q), .in2(Register_2_q), .in3(Register_3_q), .out(multiplexer_1_out),
    .sel(in_6));
  Demultiplexer #(.select(2), .width(8), .enable("false")) demultiplexer_1 (
    .out0(demultiplexer_1_out0), .out1(demultiplexer_1_out1), .out2(demultiplexer_1_out2),
    .out3(demultiplexer_1_out3), .in(multiplexer_1_out), .sel(in_7));
endmodule

module RegDT2_2 (
  input  [7:0] in_1,
  input  [7:0] in_2,
  input  [7:0] in_3,
  input  [7:0] in_4,
  input  in_5,
  input  [1:0] in_6,
  input  [1:0] in_7,
  output [7:0] out_8,
  output [7:0] out_9,
  output [7:0] out_10,
  output [7:0] out_11
);

  wire clock_1_out, decoder_1_out0, decoder_1_out1, decoder_1_out2, decoder_1_out3;
  wire [7:0] demultiplexer_1_out0, demultiplexer_1_out1, demultiplexer_1_out2, demultiplexer_1_out3,
       multiplexer_1_out, Register_0_q, Register_1_q, Register_2_q, Register_3_q;

  Clock clock_1 (.out(clock_1_out));
  Register #(.trigger("high")) Register_3 (.D(in_1), .clk(in_5), .Q(Register_3_q));  // open: en, clr
  Register Register_D (.D(demultiplexer_1_out3), .en(decoder_1_out3), .clk(clock_1_out), .Q(out_8));  // open: clr
  Register #(.trigger("high")) Register_2 (.D(in_2), .clk(in_5), .Q(Register_2_q));  // open: en, clr
  Register Register_C (.D(demultiplexer_1_out2), .en(decoder_1_out2), .clk(clock_1_out), .Q(out_9));  // open: clr
  Register #(.trigger("high")) Register_1 (.D(in_3), .clk(in_5), .Q(Register_1_q));  // open: en, clr
  Register Register_B (.D(demultiplexer_1_out1), .en(decoder_1_out1), .clk(clock_1_out), .Q(out_10));  // open: clr
  Register #(.trigger("high")) Register_0 (.D(in_4), .clk(in_5), .Q(Register_0_q));  // open: en, clr
  Register Register_A (.D(demultiplexer_1_out0), .en(decoder_1_out0), .clk(clock_1_out), .Q(out_11));  // open: clr
  Decoder #(.select(2)) decoder_1 (
    .out0(decoder_1_out0), .out1(decoder_1_out1), .out2(decoder_1_out2), .out3(decoder_1_out3), .sel(in_7));  // open: en
  Multiplexer #(.select(2), .width(8), .enable("false")) multiplexer_1 (
    .in0(Register_0_q), .in1(Register_1_q), .in2(Register_2_q), .in3(Register_3_q), .out(multiplexer_1_out),
    .sel(in_6));
  Demultiplexer #(.select(2), .width(8), .enable("false")) demultiplexer_1 (
    .out0(demultiplexer_1_out0), .out1(demultiplexer_1_out1), .out2(demultiplexer_1_out2),
    .out3(demultiplexer_1_out3), .in(multiplexer_1_out), .sel(in_7));
endmodule

module RegDT3 (
  input  [1:0] Src,
  input  [1:0] Dest,
  output [7:0] out_3,
  output [7:0] out_4,
  output [7:0] out_5,
  output [7:0] out_6
);

  wire clock_1_out, decoder_1_out0, decoder_1_out1, decoder_1_out2, decoder_1_out3;
  wire [7:0] demultiplexer_1_out0, demultiplexer_1_out1, demultiplexer_1_out2, demultiplexer_1_out3,
       multiplexer_1_out;

  Clock clock_1 (.out(clock_1_out));
  Register register_1 (.D(demultiplexer_1_out3), .en(decoder_1_out3), .clk(clock_1_out), .Q(out_3));  // open: clr
  Register register_2 (.D(demultiplexer_1_out2), .en(decoder_1_out2), .clk(clock_1_out), .Q(out_4));  // open: clr
  Register register_3 (.D(demultiplexer_1_out1), .en(decoder_1_out1), .clk(clock_1_out), .Q(out_5));  // open: clr
  Register register_4 (.D(demultiplexer_1_out0), .en(decoder_1_out0), .clk(clock_1_out), .Q(out_6));  // open: clr
  Multiplexer #(.select(2), .width(8), .enable("false")) multiplexer_1 (
    .in0(out_6), .in1(out_5), .in2(out_4), .in3(out_3), .out(multiplexer_1_out), .sel(Src));
  Decoder #(.select(2)) decoder_1 (
    .out0(decoder_1_out0), .out1(decoder_1_out1), .out2(decoder_1_out2), .out3(decoder_1_out3), .sel(Dest));  // open: en
  Demultiplexer #(.select(2), .width(8), .enable("false")) demultiplexer_1 (
    .out0(demultiplexer_1_out0), .out1(demultiplexer_1_out1), .out2(demultiplexer_1_out2),
    .out3(demultiplexer_1_out3), .in(multiplexer_1_out), .sel(Dest));
endmodule

module Accumulator (
  input  in_1,
  input  in_2,
  input  in_3,
  input  in_4,
  input  Add,
  input  Clear,
  output out_7
);

  wire adder_1_out, adder_2_cout, adder_2_out, adder_3_cout, adder_3_out, adder_4_cout, adder_4_out,
       and_1_out, clock_1_out, d_ff_1_q, d_ff_2_q, d_ff_3_q, d_ff_4_q;

  Clock clock_1 (.out(clock_1_out));
  and and_1 (and_1_out, Add, clock_1_out);
  Adder #(.width(1)) adder_1 (.a(in_1), .b(d_ff_1_q), .out(adder_1_out), .cin(adder_2_cout), .cout(out_7));
  D_Flip_Flop d_ff_1 (.D(adder_1_out), .clk(and_1_out), .Q(d_ff_1_q), .reset(Clear));  // open: Qn, preset
  Adder #(.width(1)) adder_2 (.a(in_2), .b(d_ff_2_q), .out(adder_2_out), .cin(adder_3_cout), .cout(adder_2_cout));
  D_Flip_Flop d_ff_2 (.D(adder_2_out), .clk(and_1_out), .Q(d_ff_2_q), .reset(Clear));  // open: Qn, preset
  Adder #(.width(1)) adder_3 (.a(in_3), .b(d_ff_3_q), .out(adder_3_out), .cin(adder_4_cout), .cout(adder_3_cout));
  D_Flip_Flop d_ff_3 (.D(adder_3_out), .clk(and_1_out), .Q(d_ff_3_q), .reset(Clear));  // open: Qn, preset
  Adder #(.width(1)) adder_4 (.a(in_4), .b(d_ff_4_q), .out(adder_4_out), .cin(1'b0), .cout(adder_4_cout));
  D_Flip_Flop d_ff_4 (.D(adder_4_out), .clk(and_1_out), .Q(d_ff_4_q), .reset(Clear));  // open: Qn, preset
endmodule

module Accumulator2 (
  input  [7:0] in_1,
  output out_2
);

  wire clock_1_out;
  wire [7:0] adder_1_out, register_1_q;

  Clock clock_1 (.out(clock_1_out));
  Register register_1 (.D(adder_1_out), .clk(clock_1_out), .Q(register_1_q));  // open: en, clr
  Adder adder_1 (.a(in_1), .b(register_1_q), .out(adder_1_out), .cin(1'b0), .cout(out_2));
endmodule
