// Logisim project ShiftRegisters001E.circ as structural Verilog: 5 circuits, main circuit Four_bit_Right_Shift
module Four_bit_Right_Shift (
  input  Serial_IN,
  input  Shift,
  output Serial_OUT
);

  wire and_1_out, clock_1_out, d_ff_1_q, d_ff_2_q, d_ff_3_q;

  Clock clock_1 (.out(clock_1_out));
  and and_1 (and_1_out, Shift, clock_1_out);
  D_Flip_Flop d_ff_1 (.D(Serial_IN), .clk(and_1_out), .Q(d_ff_1_q));  // open: Qn, preset, reset
  D_Flip_Flop d_ff_2 (.D(d_ff_1_q), .clk(and_1_out), .Q(d_ff_2_q));  // open: Qn, preset, reset
  D_Flip_Flop d_ff_3 (.D(d_ff_2_q), .clk(and_1_out), .Q(d_ff_3_q));  // open: Qn, preset, reset
  D_Flip_Flop d_ff_4 (.D(d_ff_3_q), .clk(and_1_out), .Q(Serial_OUT));  // open: Qn, preset, reset
endmodule

module Four_bit_Right_Shift_Cyclic (
  input  Shift
);

  wire and_1_out, clock_1_out, d_ff_1_q, d_ff_2_q, d_ff_3_q, d_ff_4_q;

  Clock clock_1 (.out(clock_1_out));
  and and_1 (and_1_out, Shift, clock_1_out);
  D_Flip_Flop d_ff_1 (.D(d_ff_4_q), .clk(and_1_out), .Q(d_ff_1_q));  // open: Qn, preset, reset
  D_Flip_Flop d_ff_2 (.D(d_ff_1_q), .clk(and_1_out), .Q(d_ff_2_q));  // open: Qn, preset, reset
  D_Flip_Flop d_ff_3 (.D(d_ff_2_q), .clk(and_1_out), .Q(d_ff_3_q));  // open: Qn, preset, reset
  D_Flip_Flop d_ff_4 (.D(d_ff_3_q), .clk(and_1_out), .Q(d_ff_4_q));  // open: Qn, preset, reset
endmodule

module Four_bit_Shift_Parallel_Load (
  input  Data,
  input  in_2,
  input  in_3,
  input  in_4,
  input  Serial_IN,
  input  Load,
  input  Shift,
  output Serial_OUT
);

  wire clock_1_out, d_ff_1_q, d_ff_2_q, d_ff_3_q, multiplexer_1_out, multiplexer_2_out, multiplexer_3_out,
       multiplexer_4_out;

  Multiplexer #(.select(2), .enable("false")) multiplexer_1 (
    .in0(d_ff_1_q), .in1(Data), .in2(Serial_IN), .in3(Serial_IN), .out(multiplexer_1_out), .sel({Shift, Load}));
  Clock clock_1 (.out(clock_1_out));
  D_Flip_Flop d_ff_1 (.D(multiplexer_1_out), .clk(clock_1_out), .Q(d_ff_1_q));  // open: Qn, preset, reset
  Multiplexer #(.select(2), .enable("false")) multiplexer_2 (
    .in0(d_ff_2_q), .in1(in_2), .in2(d_ff_1_q), .in3(d_ff_1_q), .out(multiplexer_2_out), .sel({Shift, Load}));
  D_Flip_Flop d_ff_2 (.D(multiplexer_2_out), .clk(clock_1_out), .Q(d_ff_2_q));  // open: Qn, preset, reset
  Multiplexer #(.select(2), .enable("false")) multiplexer_3 (
    .in0(d_ff_3_q), .in1(in_3), .in2(d_ff_2_q), .in3(d_ff_2_q), .out(multiplexer_3_out), .sel({Shift, Load}));
  D_Flip_Flop d_ff_3 (.D(multiplexer_3_out), .clk(clock_1_out), .Q(d_ff_3_q));  // open: Qn, preset, reset
  D_Flip_Flop d_ff_4 (.D(multiplexer_4_out), .clk(clock_1_out), .Q(Serial_OUT));  // open: Qn, preset, reset
  Multiplexer #(.select(2), .enable("false")) multiplexer_4 (
    .in0(Serial_OUT), .in1(in_4), .in2(d_ff_3_q), .in3(d_ff_3_q), .out(multiplexer_4_out), .sel({Shift, Load}));
endmodule

module Left_Shift_Reg (
  input  Reset,
  input  Load,
  input  Shift,
  input  Serial_IN,
  input  [7:0] in_5,
  output [7:0] out_6,
  output Serial_OUT
);

  wire clock_1_out;

  Clock clock_1 (.out(clock_1_out));
  // Shift_Register shift_register_1: pin names not known; wires that end beside it: Reset, Load, Shift, clock_1_out, Serial_IN, in_5[0], in_5[1], in_5[2], in_5[3], in_5[4], in_5[5], in_5[6], in_5[7], out_6[0], out_6[1], out_6[2], out_6[3], out_6[4], out_6[5], out_6[6], out_6[7]

  assign Serial_OUT = out_6[7];
endmodule

module Right_Shift_Reg (
  input  Reset,
  input  Load,
  input  Shift,
  input  Serial_IN,
  input  [7:0] in_5,
  input  [7:0] in_6,
  input  in_7,
  input  in_8,
  input  in_9,
  input  in_10,
  input  [7:0] in_11,
  output [7:0] out_12,
  output Serial_OUT,
  output out_14,
  output [7:0] out_15,
  output out_16
);

  wire clock_1_out, clock_2_out, clock_3_out;
  wire [7:0] adder_1_out, register_1_q;

  Clock clock_1 (.out(clock_1_out));
  Clock clock_2 (.out(clock_2_out));
  // Shift_Register shift_register_1: pin names not known; wires that end beside it: Reset, Load, Shift, clock_1_out, Serial_IN, in_5[7], in_5[6], in_5[5], in_5[4], in_5[3], out_12[7], out_12[6], out_12[5], out_12[4], out_12[3]
  // Shift_Register shift_register_2: pin names not known; wires that end beside it: in_5[2], in_5[1], in_5[0], in_7, in_8, in_9, clock_2_out, in_10, in_11[0], in_11[1], in_11[2], in_11[3], in_11[4], in_11[5], in_11[6], in_11[7], out_12[2], out_12[1], out_12[0], out_15[0], out_15[1], out_15[2], out_15[3], out_15[4], out_15[5], out_15[6], out_15[7]
  Clock clock_3 (.out(clock_3_out));
  Register register_1 (.D(adder_1_out), .clk(clock_3_out), .Q(register_1_q));  // open: en, clr
  Adder adder_1 (.a(in_6), .b(register_1_q), .out(adder_1_out), .cin(1'b0), .cout(out_14));

  assign out_16 = out_15[7];
  assign Serial_OUT = out_12[0];
endmodule
